# Fritzing sketch esp32_project (2) (saved by Fritzing 0.9.3b)
breadboards: 1

parts:
  ESP32_-_Back1 = ESP32 - CAM  # not connected
  U1 = ESP32-38PinWide [part_number=ESP32-38PinWide]
  U3 = LM393 [package=so08]
  DHT1 = Humidity and Temperature Sensor DHT11
  hc-sr2 = hc-sr04
  Part1 = MQ-4
  R1 = Photocell (LDR) [package=THT]
  GAS_SENSOR = GY-NEO6MV2
  J1 = Basic Servo
  R2 = Resistor [tolerance=±5% resistance=220 package=THT]

nets:
  N1: U1.GPIO27, GAS_SENSOR.Rx, R2.Pin_1
  N2: U1.GPIO14, GAS_SENSOR.Tx
  N3: U1.GND, DHT1.GND_2
  N4: U1.GPIO16, J1.pulse
  N5: U3.G1_+IN, DHT1.Vcc
  N6: U3.G1_V-, Part1.VCC
  N7: U3.G2_+IN, R1.pin_0
  N8: U3.G2_OUT, GAS_SENSOR.Vcc
  N9: U3.G1_V+, hc-sr2.VCC

notes:
  esp32 with cam
  voltage
  servo motor
  dth 11 temperature sensor
  gas sensor
  gps
  ultasonic sensor

custom parts:
  ESP32 - CAM: The ESP32-CAM has a very competitive small-size camera module that can operate independently as a minimum system with a footprint of only 27*40.5*4.5mm and a deep sleep current of up to 6mA.
  ESP32-38PinWide: Generic 38-Pin ESP32 with wide format (only access to one side of pins on a breadboard) based on Stephen Lilley's HiLetgo ESP-WROOM-32 ESP32 ESP-32S Development Board.
  Humidity and Temperature Sensor DHT11: Digital relative humidity & temperature sensor DHT11
  GY-NEO6MV2: Description: Module GPS , type GY-NEO6MV2, pour arduino et autres micro-contrôleurs. Caractéristiques De type GY-NEO6MV2 Alimentation 3V-5V Avec Flight Control EEPROM MWC Antenne large céramique, fort signal, 25 x 25 mm Paramètres de configuration sauvegardés en EEPROM Avec batterie de backup de données LED témoin de signal Module miniaturisé 25 x 35 mm Trou de fixation de 3mm Baud rate par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
